// Logisim project cpu.circ as structural Verilog: 1 circuit, main circuit cpu
module cpu (
  input  clk,
  input  [31:0] INSTRUCTION,
  input  [31:0] READ_DATA,
  output [31:0] WRITE_ADDRESS,
  output [31:0] PROGRAM_COUNTER,
  output [31:0] ra,
  output [31:0] sp,
  output [31:0] t0,
  output [31:0] t1,
  output [31:0] t2,
  output [31:0] s0,
  output [31:0] s1,
  output [31:0] a0,
  output [31:0] tohost,
  output [3:0] WRITE_ENABLE,
  output [31:0] WRITE_DATA
);

  wire Asel, BrEq, BrLt, BrUn, Bsel, comparator_1_eq, comparator_2_eq, comparator_3_eq, comparator_4_eq,
       comparator_5_eq, comparator_6_eq, comparator_7_eq, comparator_8_eq, CSRSel, CSRWen, LB, LH, MemRW,
       PCsel, RegWEn, SB, SH;
  wire [1:0] WBsel;
  wire [2:0] func3, ImmSel;
  wire [3:0] ALUSel, multiplexer_6_out, multiplexer_7_out;
  wire [6:0] func7;
  wire [24:0] INSTRUCTION2;
  wire [31:0] adder_1_out, adder_2_out, bit_extender_1_out, bit_extender_2_out, complete_Imm,
       multiplexer_1_out, multiplexer_2_out, multiplexer_3_out, multiplexer_4_out, multiplexer_5_out,
       multiplexer_9_out, PROGRAM_COUNTER2, r1, READ_DATA2, WB_data;

  Adder #(.width(32)) adder_1 (.a(PROGRAM_COUNTER), .b(32'h4), .out(adder_1_out));  // open: cin, cout
  Register #(.width(32)) PC (.D(multiplexer_1_out), .clk(clk), .Q(PROGRAM_COUNTER));  // open: en, clr
  Multiplexer #(.enable("false"), .width(32)) multiplexer_1 (
    .in0(adder_1_out), .in1(WRITE_ADDRESS), .out(multiplexer_1_out), .sel(PCsel));
  Multiplexer #(.enable("false"), .width(32)) multiplexer_2 (
    .in0(INSTRUCTION), .in1(32'h13), .out(multiplexer_2_out), .sel(PCsel));
  Comparator #(.width(7)) comparator_1 (.a(INSTRUCTION2[6:0]), .b(7'b0000011), .eq(comparator_1_eq));  // open: gt, lt
  Comparator #(.width(3)) comparator_2 (.a(func3), .b(3'b000), .eq(comparator_2_eq));  // open: gt, lt
  Comparator #(.width(7)) comparator_3 (.a(INSTRUCTION2[6:0]), .b(7'b0000011), .eq(comparator_3_eq));  // open: gt, lt
  Comparator #(.width(3)) comparator_4 (.a(func3), .b(3'b001), .eq(comparator_4_eq));  // open: gt, lt
  Comparator #(.width(7)) comparator_5 (.a(INSTRUCTION2[6:0]), .b(7'b0100011), .eq(comparator_5_eq));  // open: gt, lt
  Comparator #(.width(3)) comparator_6 (.a(func3), .b(3'b000), .eq(comparator_6_eq));  // open: gt, lt
  Comparator #(.width(7)) comparator_7 (.a(INSTRUCTION2[6:0]), .b(7'b0100011), .eq(comparator_7_eq));  // open: gt, lt
  Comparator #(.width(3)) comparator_8 (.a(func3), .b(3'b001), .eq(comparator_8_eq));  // open: gt, lt
  Register #(.width(32)) register_1 (.D(PROGRAM_COUNTER), .clk(clk), .Q(PROGRAM_COUNTER2));  // open: en, clr
  Register #(.width(32)) register_2 (
    .D(multiplexer_2_out), .clk(clk), .Q({func7, INSTRUCTION2[24:15], func3, INSTRUCTION2[11:0]}));  // open: en, clr
  and and_1 (LB, comparator_1_eq, comparator_2_eq);
  and and_2 (LH, comparator_3_eq, comparator_4_eq);
  and and_3 (SB, comparator_5_eq, comparator_6_eq);
  and and_4 (SH, comparator_7_eq, comparator_8_eq);
  control_logic control_logic_1 (
    .CSRWen(CSRWen), .PCSel(PCsel), .RegWEn(RegWEn), .ImmSel(ImmSel), .BrUn(BrUn), .ASel(Asel), .BSel(Bsel),
    .ALUSel(ALUSel), .MemRW(MemRW), .WBSel(WBsel), .CSRSel(CSRSel),
    .inst({func7, INSTRUCTION2[24:15], func3, INSTRUCTION2[11:0]}), .BrEq(BrEq), .BrLt(BrLt));
  // imm_gen imm_gen_1: pin names not known; wires that end beside it: {func7, INSTRUCTION2[24:15], func3, INSTRUCTION2[11:0]}, ImmSel, complete_Imm, r1, WRITE_DATA, BrUn
  regfile regfile_1 (
    .rs1(INSTRUCTION2[19:15]), .rs2(INSTRUCTION2[24:20]), .rd(INSTRUCTION2[11:7]), .Write_Data(WB_data),
    .RegWEn(RegWEn), .clk(clk), .ra(ra), .sp(sp), .t0(t0), .t1(t1), .t2(t2), .s0(s0), .s1(s1), .a0(a0),
    .Read_Data_1(r1), .Read_Data_2(WRITE_DATA));
  // branch_comp branch_comp_1: pin names not known; wires that end beside it: BrEq, BrLt
  Multiplexer #(.enable("false"), .width(32)) multiplexer_3 (
    .in0(r1), .in1(PROGRAM_COUNTER2), .out(multiplexer_3_out), .sel(Asel));
  Multiplexer #(.enable("false"), .width(32)) multiplexer_4 (
    .in0(WRITE_DATA), .in1(complete_Imm), .out(multiplexer_4_out), .sel(Bsel));
  alu alu_1 (.Result(WRITE_ADDRESS), .A(multiplexer_3_out), .B(multiplexer_4_out), .ALUSel(ALUSel));
  Multiplexer #(.enable("false"), .width(32)) multiplexer_5 (
    .in0(r1), .in1(complete_Imm), .out(multiplexer_5_out), .sel(CSRSel));
  Multiplexer #(.enable("false"), .width(4)) multiplexer_6 (
    .in0(4'b1111), .in1(4'b0011), .out(multiplexer_6_out), .sel(SH));
  Adder #(.width(32)) adder_2 (.a(PROGRAM_COUNTER2), .b(32'h4), .out(adder_2_out));  // open: cin, cout
  Multiplexer #(.enable("false"), .width(4)) multiplexer_7 (
    .in0(multiplexer_6_out), .in1(4'b0001), .out(multiplexer_7_out), .sel(SB));
  assign bit_extender_1_out = {{24{READ_DATA[7]}}, READ_DATA[7:0]};  // Bit_Extender bit_extender_1
  assign bit_extender_2_out = {{16{READ_DATA[15]}}, READ_DATA[15:0]};  // Bit_Extender bit_extender_2
  Multiplexer #(.enable("false"), .width(4)) multiplexer_8 (
    .in0(4'b0000), .in1(multiplexer_7_out), .out(WRITE_ENABLE), .sel(MemRW));
  Multiplexer #(.enable("false"), .width(32)) multiplexer_9 (
    .in0(READ_DATA), .in1(bit_extender_2_out), .out(multiplexer_9_out), .sel(LH));
  // csr csr_1: pin names not known; wires that end beside it: 12'h51e, multiplexer_5_out, CSRWen, clk, tohost
  Multiplexer #(.enable("false"), .select(2), .width(32)) multiplexer_10 (
    .in0(READ_DATA2), .in1(WRITE_ADDRESS), .in2(adder_2_out), .in3(complete_Imm), .out(WB_data), .sel(WBsel));
  Multiplexer #(.enable("false"), .width(32)) multiplexer_11 (
    .in0(multiplexer_9_out), .in1(bit_extender_1_out), .out(READ_DATA2), .sel(LB));

  // Other names for the same wires on the sheet: ALU_output[31:0] = WRITE_ADDRESS; opcode[6:0] = INSTRUCTION2[6:0];
  //   rd[4:0] = INSTRUCTION2[11:7]; INSTRUCTION2 (some bits) = {func7, func3}; rs1[4:0] = INSTRUCTION2[19:15];
  //   rs2[4:0] = INSTRUCTION2[24:20]; r2[31:0] = WRITE_DATA

  // Notes on the sheet:
  //   Decode
  //   Output to IMEM
  //   IMEM (do **NOT** move this)
  //   Inputs from IMEM
  //   DeBug
  //   It is OK to move the PC, RegFile, ALU, MEM, Branch Comp, Imm Gen, and Control Logic to wherever is most convenient for you when constructing your CPU, and to delete this text
  //   Inputs/Outputs for testing. Do **NOT** move these.
  //   Outputs To DMEM
  //   DMEM (do **NOT** move this)
  //   Inputs From DMEM
endmodule
